# Fritzing sketch SHADOW MSE Edition UNO Shield (saved by Fritzing 0.9.3b)
circuit board: 6.88566cm x 5.36311cm
breadboards: 1

parts:
  Motor = Dagu DGServo 9g header (male) [package=THT]
  Servo = Dagu DGServo 9g header (male) [package=THT]
  Part2 = MP3 Trigger  # not connected
  MP3_Trigger = Dagu DGServo 9g header (male) [package=THT]
  Part1 = Arduino Uno (Rev3)
  TRS1 = Audio Jack (TRS) 3.5mm [package="PG203J [THT]"]
  J1 = female pin header, 20 pins [form="♀ (female)"]

nets (from the pcb view):
  GND: Motor.gnd, Servo.gnd, MP3_Trigger.gnd, Part1.GND, TRS1.Sleeve, J1.pin19
  VCC: Motor.Vcc, Servo.Vcc, MP3_Trigger.Vcc, Part1.VIN, J1.pin20
  N1: Motor.pulse, Part1.D3_PWM
  N2: Servo.pulse, Part1.D4
  N3: MP3_Trigger.pulse, Part1.D2, J1.pin15
  N4: TRS1.Ring, J1.pin17
  N5: TRS1.Tip, J1.pin18

notes:
  GND
  VCC
  SIG
  LEFT
  RX
  TX
  RIGHT
  PIN1
